// Logisim project processador4bits.circ as structural Verilog: 4 circuits, main circuit main
module main (
  input  in_1
);

  wire CLEAR, CLK;
  wire [1:0] UC_end_dest, UC_end_op1, UC_end_op2;
  wire [2:0] UC_seletor_ula;
  wire [3:0] BancoReg_out_r2, BancoReg_out_r3, mnt0, mnt1, mnt2, mnt3, ULA_out_ula;
  wire [7:0] adder_1_out, register_1_q;
  wire [9:0] rom_1_data;

  Clock clock_1 (.out(CLK));
  Button button_1 (.out(CLEAR));
  Register register_1 (.D(adder_1_out), .Q(register_1_q), .clk(CLK), .clr(CLEAR));  // open: en
  ROM #(.dataWidth(10)) rom_1 (.addr(register_1_q), .data(rom_1_data), .sel(in_1));
  // Probe on rom_1_data
  Adder adder_1 (.a(register_1_q), .b(8'h1), .out(adder_1_out));  // open: cin, cout
  UC UC (
    .Instrucao(rom_1_data), .End_Op2(UC_end_op2), .End_Op1(UC_end_op1), .End_Dest(UC_end_dest),
    .Seletor_ULA(UC_seletor_ula));
  BancoReg BancoReg (
    .Data_In(ULA_out_ula), .Out_R2(BancoReg_out_r2), .Out_R3(BancoReg_out_r3), .End_Dest(UC_end_dest),
    .End_Op1(UC_end_op1), .End_Op2(UC_end_op2), .in_4(CLK), .Monitor_R1(mnt1), .Monitor_R0(mnt0),
    .Monitor_R2(mnt2), .Monitor_R3(mnt3));
  Hex_Digit_Display hex_digit_display_1 (.value(mnt0));  // open: dp
  Hex_Digit_Display hex_digit_display_2 (.value(mnt2));  // open: dp
  Hex_Digit_Display hex_digit_display_3 (.value(mnt1));  // open: dp
  ULA ULA (.Out_ULA(ULA_out_ula), .In_R2(BancoReg_out_r2), .In_R3(BancoReg_out_r3), .Seletor_ULA(UC_seletor_ula));
  Hex_Digit_Display hex_digit_display_4 (.value(mnt3));  // open: dp

  // Notes on the sheet:
  //   contents of rom_1 (hex, n*v repeats v):
  //   42 84 d8 2c 70 84 d8
endmodule

module ULA (
  input  [3:0] In_R2,
  input  [3:0] In_R3,
  input  [2:0] Seletor_ULA,
  output [3:0] Out_ULA
);

  wire [3:0] out0, out1, out2, out3, out4, out5, out6, out7;

  Adder #(.width(4)) adder_1 (.a(In_R2), .b(In_R3), .out(out0));  // open: cin, cout
  Subtractor #(.width(4)) subtractor_1 (.a(In_R2), .b(In_R3), .out(out1));  // open: bin, bout
  Adder #(.width(4)) adder_2 (.a(In_R2), .b(4'b0001), .out(out2));  // open: cin, cout
  Subtractor #(.width(4)) subtractor_2 (.a(In_R2), .b(4'b0001), .out(out3));  // open: bin, bout
  assign out7 = ~In_R2;  // NOT_Gate not_1, 4 bits wide
  assign out4 = In_R2 & In_R3;  // AND_Gate and_1, 4 bits wide
  assign out5 = In_R2 | In_R3;  // OR_Gate or_1, 4 bits wide
  assign out6 = In_R2 ^ In_R3;  // XOR_Gate xor_1, 4 bits wide
  Multiplexer #(.select(3), .width(4), .enable("false")) multiplexer_1 (
    .in0(out0), .in1(out1), .in2(out2), .in3(out3), .in4(out4), .in5(out5), .in6(out6), .in7(out7),
    .out(Out_ULA), .sel(Seletor_ULA));
endmodule

module BancoReg (
  input  [3:0] Data_In,
  input  [1:0] End_Op1,
  input  [1:0] End_Op2,
  input  in_4,
  input  [1:0] End_Dest,
  output [3:0] Monitor_R0,
  output [3:0] Out_R2,
  output [3:0] Monitor_R1,
  output [3:0] Out_R3,
  output [3:0] Monitor_R2,
  output [3:0] Monitor_R3
);

  wire outdec0, outdec1, outdec2, outdec3;

  Decoder #(.select(2), .enable("false")) decoder_1 (
    .out0(outdec0), .out1(outdec1), .out2(outdec2), .out3(outdec3), .sel(End_Dest));
  Register #(.width(4)) R0 (.D(Data_In), .en(outdec0), .Q(Monitor_R0), .clk(in_4));  // open: clr
  Register #(.width(4)) R1 (.D(Data_In), .en(outdec1), .Q(Monitor_R1), .clk(in_4));  // open: clr
  Register #(.width(4)) R2 (.D(Data_In), .en(outdec2), .Q(Monitor_R2), .clk(in_4));  // open: clr
  Register #(.width(4)) R3 (.D(Data_In), .en(outdec3), .Q(Monitor_R3), .clk(in_4));  // open: clr
  Multiplexer #(.select(2), .width(4), .enable("false")) multiplexer_1 (
    .in0(Monitor_R0), .in1(Monitor_R1), .in2(Monitor_R2), .in3(Monitor_R3), .out(Out_R2), .sel(End_Op1));
  Multiplexer #(.select(2), .width(4), .enable("false")) multiplexer_2 (
    .in0(Monitor_R0), .in1(Monitor_R1), .in2(Monitor_R2), .in3(Monitor_R3), .out(Out_R3), .sel(End_Op2));

  // Other names for the same wires on the sheet: CLK = in_4; out_R0[3:0] = Monitor_R0; out_R1[3:0] = Monitor_R1;
  //   out_R2_t[3:0] = Monitor_R2; out_R3_t[3:0] = Monitor_R3
endmodule

module UC (
  input  [9:0] Instrucao,
  output [1:0] End_Op2,
  output [1:0] End_Op1,
  output [1:0] End_Dest,
  output [2:0] Seletor_ULA
);


  assign End_Dest = Instrucao[7:6];
  assign End_Op1 = Instrucao[5:4];
  assign End_Op2 = Instrucao[3:2];
  assign Seletor_ULA = {Instrucao[8], Instrucao[1:0]};
endmodule
